// Logisim project GISC-1.2.circ as structural Verilog: 1 circuit, main circuit main
module main (
);

  wire and_1_out, and_2_out, and_3_out, and_5_out, and_6_out, and_7_out, and_8_out, clock_1_out,
       comparator_2_lt, comparator_3_gt, comparator_4_eq, comparator_5_eq, comparator_5_gt, d_ff_1_q,
       d_ff_2_q, d_ff_3_q, decoder_1_out7, decoder_1_out8, decoder_1_out9, decoder_2_out1, decoder_2_out2,
       decoder_2_out3, decoder_2_out4, decoder_2_out5, decoder_2_out6, decoder_2_out7, decoder_2_out8,
       decoder_2_out9, decoder_2_out10, decoder_2_out11, decoder_2_out12, decoder_2_out13, decoder_2_out14,
       decoder_3_out0, decoder_3_out1, decoder_3_out2, decoder_3_out3, decoder_3_out4, decoder_4_out0,
       decoder_4_out1, decoder_4_out2, decoder_4_out3, decoder_4_out4, not_1_out, not_2_out, or_1_out,
       register_2_q, transistor_1_out, transistor_2_out, transistor_4_out, transistor_6_out,
       transistor_7_out, transistor_9_out, transistor_17_out, transistor_18_out, transistor_21_out,
       transistor_24_out;
  wire [3:0] controlled_buffer_4_out_2, controlled_buffer_4_out_3, controlled_buffer_5_out,
       controlled_buffer_5_out_2, controlled_buffer_6_out, controlled_buffer_7_out, multiplexer_1_out,
       register_1_q, rom_1_data_2, rom_1_data_3, subtractor_1_out, subtractor_2_out;
  wire [6:0] bit_extender_3_out;
  wire [7:0] _01_q, _02_q, _03_q, _04_q, ACC_q, adder_1_out, bit_extender_1_out, bit_extender_2_out,
       controlled_buffer_4_out, controlled_buffer_8_out, controlled_buffer_10_out, controlled_buffer_11_out,
       controlled_buffer_13_out, counter_1_q, multiplexer_2_out, multiplexer_3_out, multiplexer_4_out,
       multiplexer_5_out, multiplexer_6_out, multiplexer_7_out, multiplexer_8_out, multiplexer_9_out,
       multiplexer_10_out, multiplexer_11_out, ram_1_data, rom_1_data, subtractor_3_out, transistor_3_out,
       transistor_8_out, transistor_15_out, transistor_16_out, transistor_19_out, transistor_20_out;
  wire [15:0] controlled_buffer_1_out, controlled_buffer_3_out, controlled_buffer_9_out;

  or or_1 (or_1_out, not_1_out, comparator_5_gt);
  and and_1 (and_1_out, decoder_2_out11, or_1_out);
  Transistor transistor_1 (.in(and_1_out), .out(transistor_1_out), .gate(register_2_q));
  Transistor #(.\type ("n"), .gate("br")) transistor_2 (
    .in(transistor_1_out), .out(transistor_2_out), .gate(transistor_1_out));
  Multiplexer #(.width(4)) multiplexer_1 (
    .in0(subtractor_2_out), .in1(subtractor_1_out), .out(multiplexer_1_out), .sel(and_2_out));  // open: en
  Transistor #(.\type ("n"), .gate("br"), .width(8)) transistor_3 (
    .in(controlled_buffer_3_out[11:4]), .out(transistor_3_out), .gate(transistor_1_out));
  Transistor #(.\type ("n")) transistor_4 (.in(transistor_2_out), .out(transistor_4_out), .gate(transistor_2_out));
  Transistor #(.gate("br"), .width(8)) transistor_5 (
    .in(bit_extender_1_out), .out(transistor_3_out), .gate(transistor_1_out));
  assign bit_extender_1_out = {{4{1'b0}}, controlled_buffer_1_out[11:8]};  // Bit_Extender bit_extender_1
  Decoder #(.select(4)) decoder_1 (
    .out7(decoder_1_out7), .out8(decoder_1_out8), .out9(decoder_1_out9), .sel(controlled_buffer_4_out_3));  // open: out0, out1, out2, out3, out4, out5, out6, out10, out11, out12, out13, out14, out15, en
  assign controlled_buffer_1_out = decoder_2_out10 ? {rom_1_data_3, rom_1_data_2, rom_1_data} : 16'bz;  // Controlled_Buffer controlled_buffer_1
  Comparator comparator_1 (.a(multiplexer_4_out), .b(multiplexer_7_out), .eq(transistor_2_out));  // open: gt, lt
  Subtractor #(.width(4)) subtractor_1 (
    .a(controlled_buffer_3_out[3:0]), .b(4'b0001), .out(subtractor_1_out));  // open: bin, bout
  not not_1 (not_1_out, d_ff_1_q);
  and and_2 (and_2_out, not_1_out, comparator_5_eq);
  D_Flip_Flop d_ff_1 (.clk(decoder_2_out11), .D(1'b1), .Q(d_ff_1_q), .reset(comparator_5_eq));  // open: Qn, preset, en
  Subtractor #(.width(4)) subtractor_2 (.a(register_1_q), .b(4'b0001), .out(subtractor_2_out));  // open: bin, bout
  Transistor #(.\type ("n"), .gate("br")) transistor_6 (
    .in(transistor_4_out), .out(transistor_6_out), .gate(transistor_4_out));
  Transistor #(.gate("br")) transistor_7 (.in(transistor_9_out), .out(transistor_7_out), .gate(transistor_4_out));
  Transistor #(.\type ("n"), .gate("br"), .width(8)) transistor_8 (
    .in(transistor_3_out), .out(transistor_8_out), .gate(transistor_4_out));
  Comparator comparator_2 (.a(multiplexer_2_out), .b({8{1'b0}}), .lt(comparator_2_lt));  // open: gt, eq
  Transistor #(.\type ("n"), .gate("br")) transistor_9 (
    .in(comparator_2_lt), .out(transistor_9_out), .gate(decoder_1_out9));
  Transistor #(.\type ("n"), .gate("br")) transistor_10 (
    .in(comparator_3_gt), .out(transistor_9_out), .gate(decoder_1_out8));
  Comparator comparator_3 (.a(multiplexer_2_out), .b({8{1'b1}}), .gt(comparator_3_gt));  // open: eq, lt
  Transistor #(.\type ("n"), .gate("br")) transistor_11 (
    .in(comparator_4_eq), .out(transistor_9_out), .gate(decoder_1_out7));
  Comparator comparator_4 (.a(multiplexer_2_out), .b({8{1'b0}}), .eq(comparator_4_eq));  // open: gt, lt
  Register #(.width(4)) register_1 (
    .D(multiplexer_1_out), .en(decoder_2_out11), .Q(register_1_q), .clk(transistor_18_out), .clr(and_3_out));
  Comparator #(.width(4)) comparator_5 (
    .a(register_1_q), .b(4'b0000), .gt(comparator_5_gt), .eq(comparator_5_eq));  // open: lt
  Transistor #(.\type ("n")) transistor_12 (.in(decoder_2_out6), .out(transistor_6_out), .gate(decoder_2_out6));
  Transistor #(.\type ("n")) transistor_13 (.in(transistor_7_out), .out(transistor_6_out), .gate(transistor_7_out));
  Transistor #(.width(8)) transistor_14 (.in(transistor_15_out), .out(transistor_8_out), .gate(transistor_4_out));
  Transistor #(.\type ("n"), .gate("br"), .width(8)) transistor_15 (
    .in(controlled_buffer_4_out), .out(transistor_15_out), .gate(transistor_9_out));
  assign transistor_15_out = transistor_6_out ? rom_1_data : 8'bz;  // Controlled_Buffer controlled_buffer_2
  Register #(.width(1)) register_2 (
    .D(comparator_5_eq), .Q(register_2_q), .clk(comparator_5_eq), .clr(and_3_out));  // open: en
  Transistor #(.\type ("n"), .gate("br"), .width(8)) transistor_16 (
    .in(multiplexer_5_out), .out(transistor_16_out), .gate(decoder_2_out12));
  not not_2 (not_2_out, transistor_6_out);
  assign controlled_buffer_3_out = decoder_2_out11 ? {rom_1_data_3, rom_1_data_2, rom_1_data} : 16'bz;  // Controlled_Buffer controlled_buffer_3
  assign {controlled_buffer_4_out_3, controlled_buffer_4_out_2, controlled_buffer_4_out} = transistor_24_out ? {rom_1_data_3, rom_1_data_2, rom_1_data} : 16'bz;  // Controlled_Buffer controlled_buffer_4
  Multiplexer #(.select(4), .width(8)) multiplexer_2 (
    .in0(ACC_q), .in1(_01_q), .in2(_02_q), .in3(_03_q), .in4(_04_q), .out(multiplexer_2_out),
    .sel(controlled_buffer_4_out_2));  // open: in5, in6, in7, in8, in9, in10, in11, in12, in13, in14, in15, en
  Multiplexer #(.select(4), .width(8)) multiplexer_3 (
    .in0(ACC_q), .in1(_01_q), .in2(_02_q), .in3(_03_q), .in4(_04_q), .out(multiplexer_3_out),
    .sel(controlled_buffer_8_out[3:0]));  // open: in5, in6, in7, in8, in9, in10, in11, in12, in13, in14, in15, en
  Multiplexer #(.select(4), .width(8)) multiplexer_4 (
    .in0(ACC_q), .in1(_01_q), .in2(_02_q), .in3(_03_q), .in4(_04_q), .out(multiplexer_4_out),
    .sel(controlled_buffer_1_out[3:0]));  // open: in5, in6, in7, in8, in9, in10, in11, in12, in13, in14, in15, en
  and and_3 (and_3_out, d_ff_2_q, d_ff_3_q);
  assign bit_extender_2_out = {{4{1'b0}}, controlled_buffer_5_out_2};  // Bit_Extender bit_extender_2
  Transistor #(.\type ("n")) transistor_17 (.in(decoder_2_out12), .out(transistor_17_out), .gate(decoder_2_out12));
  Transistor transistor_18 (.in(clock_1_out), .out(transistor_18_out), .gate(decoder_2_out13));
  Clock clock_1 (.out(clock_1_out));
  D_Flip_Flop d_ff_2 (.clk(transistor_18_out), .D(register_2_q), .Q(d_ff_2_q));  // open: Qn, preset, en, reset
  D_Flip_Flop d_ff_3 (.clk(transistor_18_out), .D(decoder_2_out11), .Q(d_ff_3_q));  // open: Qn, preset, en, reset
  Counter counter_1 (
    .load(transistor_6_out), .D(transistor_8_out), .count(not_2_out), .Q(counter_1_q), .clk(transistor_18_out));  // open: carry, clr
  Multiplexer #(.select(4), .width(8)) multiplexer_5 (
    .in0(ACC_q), .in1(_01_q), .in2(_02_q), .in3(_03_q), .in4(_04_q), .out(multiplexer_5_out),
    .sel(controlled_buffer_5_out));  // open: in5, in6, in7, in8, in9, in10, in11, in12, in13, in14, in15, en
  Multiplexer #(.select(4), .width(8)) multiplexer_6 (
    .in0(ACC_q), .in1(_01_q), .in2(_02_q), .in3(_03_q), .in4(_04_q), .out(multiplexer_6_out),
    .sel(controlled_buffer_8_out[7:4]));  // open: in5, in6, in7, in8, in9, in10, in11, in12, in13, in14, in15, en
  Transistor #(.\type ("n"), .gate("br"), .width(8)) transistor_19 (
    .in(ram_1_data), .out(transistor_19_out), .gate(decoder_2_out5));
  RAM #(.bus("separate")) ram_1 (
    .addr(bit_extender_2_out), .din(transistor_16_out), .data(ram_1_data), .str(transistor_17_out),
    .clk(transistor_18_out), .ld(decoder_2_out5));  // open: sel, clr
  assign {controlled_buffer_5_out_2, controlled_buffer_5_out} = decoder_2_out12 ? rom_1_data : 8'bz;  // Controlled_Buffer controlled_buffer_5
  ROM #(.dataWidth(16)) rom_1 (.addr(counter_1_q), .data({rom_1_data_3, rom_1_data_2, rom_1_data}));  // open: sel
  Subtractor subtractor_3 (.a(multiplexer_6_out), .b(multiplexer_3_out), .out(subtractor_3_out));  // open: bin, bout
  Multiplexer #(.select(4), .width(8)) multiplexer_7 (
    .in0(ACC_q), .in1(_01_q), .in2(_02_q), .in3(_03_q), .in4(_04_q), .out(multiplexer_7_out),
    .sel(controlled_buffer_1_out[7:4]));  // open: in5, in6, in7, in8, in9, in10, in11, in12, in13, in14, in15, en
  assign {controlled_buffer_6_out, controlled_buffer_5_out_2} = decoder_2_out5 ? rom_1_data : 8'bz;  // Controlled_Buffer controlled_buffer_6
  assign {controlled_buffer_6_out, controlled_buffer_7_out} = decoder_2_out4 ? rom_1_data : 8'bz;  // Controlled_Buffer controlled_buffer_7
  assign controlled_buffer_8_out = decoder_2_out3 ? rom_1_data : 8'bz;  // Controlled_Buffer controlled_buffer_8
  assign controlled_buffer_9_out = decoder_2_out14 ? {rom_1_data_3, rom_1_data_2, rom_1_data} : 16'bz;  // Controlled_Buffer controlled_buffer_9
  assign controlled_buffer_10_out = decoder_2_out2 ? rom_1_data : 8'bz;  // Controlled_Buffer controlled_buffer_10
  Transistor #(.\type ("n"), .width(8)) transistor_20 (
    .in(subtractor_3_out), .out(transistor_20_out), .gate(decoder_2_out3));
  Multiplexer #(.select(4), .width(8)) multiplexer_8 (
    .in0(ACC_q), .in1(_01_q), .in2(_02_q), .in3(_03_q), .in4(_04_q), .out(multiplexer_8_out),
    .sel(controlled_buffer_10_out[7:4]));  // open: in5, in6, in7, in8, in9, in10, in11, in12, in13, in14, in15, en
  Decoder #(.select(4)) decoder_2 (
    .out1(decoder_2_out1), .out2(decoder_2_out2), .out3(decoder_2_out3), .out4(decoder_2_out4),
    .out5(decoder_2_out5), .out6(decoder_2_out6), .out7(decoder_2_out7), .out8(decoder_2_out8),
    .out9(decoder_2_out9), .out10(decoder_2_out10), .out11(decoder_2_out11), .out12(decoder_2_out12),
    .out13(decoder_2_out13), .out14(decoder_2_out14), .sel(rom_1_data_3));  // open: out0, out15, en
  assign controlled_buffer_11_out = decoder_2_out1 ? rom_1_data : 8'bz;  // Controlled_Buffer controlled_buffer_11
  assign transistor_20_out = decoder_2_out1 ? controlled_buffer_11_out : 8'bz;  // Controlled_Buffer controlled_buffer_12
  Transistor #(.\type ("n")) transistor_21 (.in(decoder_2_out2), .out(transistor_21_out), .gate(decoder_2_out2));
  Transistor #(.\type ("n"), .width(8)) transistor_22 (
    .in(adder_1_out), .out(transistor_20_out), .gate(decoder_2_out2));
  and and_4 (transistor_21_out, decoder_2_out1, decoder_3_out0);
  Transistor #(.\type ("n")) transistor_23 (.in(decoder_2_out3), .out(transistor_21_out), .gate(decoder_2_out3));
  Transistor #(.\type ("n"), .gate("br")) transistor_24 (
    .in(decoder_2_out7), .out(transistor_24_out), .gate(decoder_2_out7));
  and and_5 (and_5_out, decoder_2_out1, decoder_3_out1);
  Register ACC (.D(transistor_20_out), .en(transistor_21_out), .Q(ACC_q), .clk(transistor_18_out));  // open: clr
  Multiplexer #(.select(4), .width(8)) multiplexer_9 (
    .in0(ACC_q), .in1(_01_q), .in2(_02_q), .in3(_03_q), .in4(_04_q), .out(multiplexer_9_out),
    .sel(controlled_buffer_10_out[3:0]));  // open: in5, in6, in7, in8, in9, in10, in11, in12, in13, in14, in15, en
  Multiplexer #(.select(4), .width(8)) multiplexer_10 (
    .in0(ACC_q), .in1(_01_q), .in2(_02_q), .in3(_03_q), .in4(_04_q), .out(multiplexer_10_out),
    .sel(controlled_buffer_9_out[3:0]));  // open: in5, in6, in7, in8, in9, in10, in11, in12, in13, in14, in15, en
  Transistor #(.\type ("n")) transistor_25 (.in(decoder_2_out9), .out(transistor_24_out), .gate(decoder_2_out9));
  Transistor #(.\type ("n")) transistor_26 (.in(decoder_2_out8), .out(transistor_24_out), .gate(decoder_2_out8));
  Decoder #(.select(4)) decoder_3 (
    .out0(decoder_3_out0), .out1(decoder_3_out1), .out2(decoder_3_out2), .out3(decoder_3_out3),
    .out4(decoder_3_out4), .sel(rom_1_data_2));  // open: out5, out6, out7, out8, out9, out10, out11, out12, out13, out14, out15, en
  Register _01 (.D(controlled_buffer_11_out), .en(and_5_out), .Q(_01_q), .clk(transistor_18_out));  // open: clr
  Adder adder_1 (.a(multiplexer_9_out), .b(multiplexer_8_out), .out(adder_1_out));  // open: cin, cout
  Bit_Extender #(.out_width(7)) bit_extender_3 (.in(multiplexer_10_out), .out(bit_extender_3_out));
  and and_6 (and_6_out, decoder_2_out1, decoder_3_out2);
  Register _02 (.D(controlled_buffer_11_out), .en(and_6_out), .Q(_02_q), .clk(transistor_18_out));  // open: clr
  Transistor #(.\type ("n")) transistor_27 (.in(decoder_4_out2), .out(and_6_out), .gate(decoder_4_out2));
  Transistor #(.\type ("n")) transistor_28 (.in(decoder_4_out1), .out(and_5_out), .gate(decoder_4_out1));
  Transistor #(.\type ("n")) transistor_29 (.in(decoder_4_out0), .out(transistor_21_out), .gate(decoder_4_out0));
  TTY tty_1 (.data(bit_extender_3_out), .clk(transistor_18_out), .we(decoder_2_out14));  // open: clr
  and and_7 (and_7_out, decoder_2_out1, decoder_3_out3);
  Register _03 (.D(controlled_buffer_11_out), .en(and_7_out), .Q(_03_q), .clk(transistor_18_out));  // open: clr
  Transistor #(.\type ("n")) transistor_30 (.in(decoder_4_out3), .out(and_7_out), .gate(decoder_4_out3));
  and and_8 (and_8_out, decoder_2_out1, decoder_3_out4);
  Transistor #(.\type ("n")) transistor_31 (.in(decoder_4_out4), .out(and_8_out), .gate(decoder_4_out4));
  Decoder #(.select(4)) decoder_4 (
    .out0(decoder_4_out0), .out1(decoder_4_out1), .out2(decoder_4_out2), .out3(decoder_4_out3),
    .out4(decoder_4_out4), .sel(controlled_buffer_6_out));  // open: out5, out6, out7, out8, out9, out10, out11, out12, out13, out14, out15, en
  Register _04 (.D(controlled_buffer_11_out), .en(and_8_out), .Q(_04_q), .clk(transistor_18_out));  // open: clr
  Multiplexer #(.select(4), .width(8)) multiplexer_11 (
    .in0(ACC_q), .in1(_01_q), .in2(_02_q), .in3(_03_q), .in4(_04_q), .out(multiplexer_11_out),
    .sel(controlled_buffer_7_out));  // open: in5, in6, in7, in8, in9, in10, in11, in12, in13, in14, in15, en
  Transistor #(.\type ("n"), .width(8)) transistor_32 (
    .in(controlled_buffer_13_out), .out(controlled_buffer_11_out), .gate(decoder_4_out1));
  Transistor #(.\type ("n"), .width(8)) transistor_33 (
    .in(controlled_buffer_13_out), .out(adder_1_out), .gate(decoder_4_out0));
  assign controlled_buffer_13_out = decoder_2_out4 ? multiplexer_11_out : 8'bz;  // Controlled_Buffer controlled_buffer_13
  Transistor #(.\type ("n"), .width(8)) transistor_34 (
    .in(controlled_buffer_13_out), .out(controlled_buffer_11_out), .gate(decoder_4_out3));
  Transistor #(.\type ("n"), .width(8)) transistor_35 (
    .in(controlled_buffer_13_out), .out(controlled_buffer_11_out), .gate(decoder_4_out2));
  Transistor #(.\type ("n"), .width(8)) transistor_36 (
    .in(controlled_buffer_13_out), .out(controlled_buffer_11_out), .gate(decoder_4_out4));
  assign controlled_buffer_13_out = decoder_2_out5 ? transistor_19_out : 8'bz;  // Controlled_Buffer controlled_buffer_14

  // Notes on the sheet:
  //   contents of rom_1 (hex, n*v repeats v):
  //   1004 1112 1002 1005 1107 2001 1309 2021 3031 0 1005 0 3031 0 1312 1106 0 3031 4040 0 c0c3 502c 1300
  //   0 7360 9380 1302 4023 0 b1c5 0 0 0 b205 1052 e000
endmodule
